# Fritzing sketch raspberrypi (saved by Fritzing 0.9.2b)
breadboards: 1

parts:
  Raspberry_Pi1 = Raspberry Pi 2
  NRF24L3 = NRF24L01

nets:
  3V3: Raspberry_Pi1.3V3, NRF24L3.VCC
  N1: Raspberry_Pi1.GPIO10, NRF24L3.MOSI
  N2: Raspberry_Pi1.GPIO9, NRF24L3.MISO
  N3: Raspberry_Pi1.GPIO11, NRF24L3.SCK
  N4: Raspberry_Pi1.GPIO8, NRF24L3.CE
  N5: Raspberry_Pi1.GPIO25, NRF24L3.CSN
  GND: Raspberry_Pi1.GND, NRF24L3.GND

custom parts:
  NRF24L01: NRF24L01 module
